# Fritzing sketch 4D_Brachiosaurus (saved by Fritzing 0.9.2b)
breadboards: 1

parts:
  Raspberry_Pi1 = Raspberry Pi 2
  IC1 = L293D [package=THT]
  S1 = Pushbutton [package="[THT]"]
  S2 = Pushbutton [package="[THT]"]
  M2 = DC Motor
  VCC2 = 4 x AAA Battery Mount

nets:
  N1: Raspberry_Pi1.GPIO9, S2.Pin_3, S2.Pin_4
  N2: Raspberry_Pi1.GND, IC1.0V, S1.Pin_1, S1.Pin_2, S2.Pin_1, S2.Pin_2, VCC2.-
  N3: Raspberry_Pi1.GPIO25, S1.Pin_3, S1.Pin_4
  N4: Raspberry_Pi1.GPIO24, IC1.Enable_1
  N5: Raspberry_Pi1.GPIO23, IC1.In_1
  N6: Raspberry_Pi1.GPIO18, IC1.In_2
  N7: Raspberry_Pi1.5V, IC1.+V
  N8: IC1.Out_1_(_Controlled_by_Enable_1_), M2.pin_2
  N9: IC1.Out_2_(_Controlled_by_Enable_1_), M2.pin_1
  N10: IC1.+Vmotor, VCC2.+
